// Logisim project 4-Bit Comparator 四位数据比较器.circ as structural Verilog: 1 circuit, main circuit main
module main (
);

  wire and_1_out, and_2_out, and_3_out, and_4_out, Equal, Great, Less, not_1_out, not_2_out, not_3_out,
       not_4_out, X0, X1, X2, X3, xnor_1_out, xnor_2_out, xnor_3_out, xnor_4_out, Y0, Y1, Y2, Y3;

  xnor xnor_1 (xnor_1_out, X3, Y3);
  xnor xnor_2 (xnor_2_out, X2, Y2);
  xnor xnor_3 (xnor_3_out, X1, Y1);
  xnor xnor_4 (xnor_4_out, X0, Y0);
  not not_1 (not_1_out, Y3);
  not not_2 (not_2_out, Y2);
  not not_3 (not_3_out, Y1);
  not not_4 (not_4_out, Y0);
  and and_1 (and_1_out, not_1_out, X3);
  and and_2 (and_2_out, xnor_1_out, not_2_out, X2);
  and and_3 (and_3_out, xnor_1_out, xnor_2_out, not_3_out, X1);
  and and_4 (and_4_out, xnor_1_out, xnor_2_out, xnor_3_out, not_4_out, X0);
  and and_5 (Equal, xnor_1_out, xnor_2_out, xnor_3_out, xnor_4_out);
  or or_1 (Great, and_1_out, and_2_out, and_3_out, and_4_out);
  nor nor_1 (Less, Equal, Great);
endmodule
