// Logisim project 8-Bit Adder 八位加法器.circ as structural Verilog: 1 circuit, main circuit main
module main (
);

  wire adder_1_cout, adder_2_cout, adder_3_cout, adder_4_cout, adder_5_cout, adder_6_cout, adder_7_cout,
       adder_8_cout;
  wire [7:0] _0, xor_1_out, xor_2_out, xor_3_out, xor_4_out, xor_5_out, xor_6_out, xor_7_out, xor_8_out;

  xor xor_1 (xor_1_out[0], _0[0], _0[0]);
  xor xor_2 (xor_2_out[0], _0[0], _0[0]);
  xor xor_3 (xor_3_out[0], _0[0], _0[0]);
  xor xor_4 (xor_4_out[0], _0[0], _0[0]);
  xor xor_5 (xor_5_out[0], _0[0], _0[0]);
  buf xor_6 (xor_6_out[0], _0[0]);  // XOR_Gate
  xor xor_7 (xor_7_out[0], _0[0], _0[0]);
  xor xor_8 (xor_8_out[0], _0[0], _0[0]);
  Adder adder_1 (.a(_0), .b(xor_1_out), .out(_0), .cin(_0[0]), .cout(adder_1_cout));
  Adder adder_2 (.a(_0), .b(xor_2_out), .out(_0), .cin(adder_1_cout), .cout(adder_2_cout));
  Adder adder_3 (.a(_0), .b(xor_3_out), .out(_0), .cin(adder_2_cout), .cout(adder_3_cout));
  Adder adder_4 (.a(_0), .b(xor_4_out), .out(_0), .cin(adder_3_cout), .cout(adder_4_cout));
  Adder adder_5 (.a(_0), .b(xor_5_out), .out(_0), .cin(adder_4_cout), .cout(adder_5_cout));
  Adder adder_6 (.a(_0), .b(xor_6_out), .out(_0), .cin(adder_5_cout), .cout(adder_6_cout));
  Adder adder_7 (.a(_0), .b(xor_7_out), .out(_0), .cin(adder_6_cout), .cout(adder_7_cout));
  Adder adder_8 (.a(_0), .b(xor_8_out), .out(_0), .cin(adder_7_cout), .cout(adder_8_cout));
  xor xor_9 (_0[0], adder_7_cout, adder_8_cout);
  // Pins of 1 and 8 bits meet at _0
  // Pins of 1 and 8 bits meet at xor_5_out
  // Pins of 1 and 8 bits meet at xor_4_out
  // Pins of 1 and 8 bits meet at xor_8_out
  // Pins of 1 and 8 bits meet at xor_3_out
  // Pins of 1 and 8 bits meet at xor_7_out
  // Pins of 1 and 8 bits meet at xor_6_out
  // Pins of 1 and 8 bits meet at xor_2_out
  // Pins of 1 and 8 bits meet at xor_1_out

  // Notes on the sheet:
  //   x0
  //   Control
  //   s0
  //   s7
  //   flow
endmodule
