// Logisim project 多路选择器型比较控制器 .circ as structural Verilog: 1 circuit, main circuit main
module main (
  input  [7:0] in_1,
  input  T2,
  input  T1
);

  wire A_qn, and_1_out, and_2_out, and_3_out, and_4_out, and_5_out, and_6_out, B_qn, CAP_out,
       comparator_1_gt, LDA_out, LDB1_out, LDB2_out, multiplexer_1_out, multiplexer_2_out, not_1_out,
       or_1_out;
  wire [1:0] A_q;
  wire [7:0] A_2_q, B_2_q, controlled_buffer_1_out, controlled_buffer_2_out;

  not not_1 (not_1_out, comparator_1_gt);
  and and_1 (and_1_out, 1'b1, comparator_1_gt);
  and and_2 (and_2_out, 1'b1, not_1_out);
  Multiplexer #(.select(2)) multiplexer_1 (
    .in0(1'b0), .in1(1'b1), .in2(1'b1), .in3(and_1_out), .out(multiplexer_1_out), .sel(A_q), .en(1'b1));
  Multiplexer #(.select(2)) multiplexer_2 (
    .in0(1'b1), .in1(1'b1), .in2(1'b0), .in3(and_2_out), .out(multiplexer_2_out), .sel(A_q), .en(1'b1));
  D_Flip_Flop A (.clk(T1), .D(multiplexer_1_out), .Q(A_q[0]), .Qn(A_qn));  // open: preset, en, reset
  D_Flip_Flop B (.clk(T1), .D(multiplexer_2_out), .Q(A_q[1]), .Qn(B_qn));  // open: preset, en, reset
  and LDB1 (LDB1_out, A_qn, B_qn);
  and LDA (LDA_out, A_qn, A_q[1]);
  Register A_2 (.D(B_2_q), .Q(A_2_q), .clk(and_4_out));  // open: en, clr
  and and_3 (and_3_out, T2, CAP_out);
  and and_4 (and_4_out, T2, LDA_out);
  and LDB2 (LDB2_out, A_q[0], B_qn);
  assign controlled_buffer_1_out = and_3_out ? A_2_q : 8'bz;  // Controlled_Buffer controlled_buffer_1
  and CAP (CAP_out, A_q[0], A_q[1]);
  Register B_2 (.D(in_1), .Q(B_2_q), .clk(and_5_out));  // open: en, clr
  and and_5 (and_5_out, T2, or_1_out);
  or or_1 (or_1_out, LDB1_out, LDB2_out);
  and and_6 (and_6_out, T2, CAP_out);
  assign controlled_buffer_2_out = and_6_out ? B_2_q : 8'bz;  // Controlled_Buffer controlled_buffer_2
  Comparator comparator_1 (
    .a(controlled_buffer_1_out), .b(controlled_buffer_2_out), .gt(comparator_1_gt));  // open: eq, lt
endmodule
