// Logisim project 定序型比较控制器 .circ as structural Verilog: 1 circuit, main circuit main
module main (
  input  [7:0] in_1,
  input  in_2,
  input  in_3
);

  wire a_q, a_qn, and_1_out, and_2_out, and_3_out, b_q, b_qn, c_q, c_qn, comparator_1_gt, d_q, d_qn, LDA_out,
       LDB1_out, not_1_out, or_1_out, or_2_out, or_3_out;
  wire [7:0] A_2_q, B_2_q, controlled_buffer_1_out, controlled_buffer_2_out;

  and and_1 (and_1_out, d_qn, c_qn, b_qn, a_qn);
  D_Flip_Flop a (.clk(in_3), .D(and_1_out), .Q(a_q), .Qn(a_qn));  // open: preset, en, reset
  not not_1 (not_1_out, comparator_1_gt);
  or or_1 (or_1_out, a_q, and_2_out);
  and and_2 (and_2_out, d_q, not_1_out);
  D_Flip_Flop b (.clk(in_3), .D(or_1_out), .Q(b_q), .Qn(b_qn));  // open: preset, en, reset
  and and_3 (and_3_out, d_q, comparator_1_gt);
  or or_2 (or_2_out, b_q, and_3_out);
  D_Flip_Flop c (.clk(in_3), .D(or_2_out), .Q(c_q), .Qn(c_qn));  // open: preset, en, reset
  D_Flip_Flop d (.clk(in_3), .D(c_q), .Q(d_q), .Qn(d_qn));  // open: preset, en, reset
  and LDB1 (LDB1_out, in_2, or_3_out);
  or or_3 (or_3_out, a_q, c_q);
  Register A_2 (.D(B_2_q), .Q(A_2_q), .clk(LDA_out));  // open: en, clr
  and LDA (LDA_out, in_2, b_q);
  assign controlled_buffer_1_out = d_q ? A_2_q : 8'bz;  // Controlled_Buffer controlled_buffer_1
  Register B_2 (.D(in_1), .Q(B_2_q), .clk(LDB1_out));  // open: en, clr
  assign controlled_buffer_2_out = d_q ? B_2_q : 8'bz;  // Controlled_Buffer controlled_buffer_2
  Comparator comparator_1 (
    .a(controlled_buffer_1_out), .b(controlled_buffer_2_out), .gt(comparator_1_gt));  // open: eq, lt
endmodule
