// Logisim project 计数器型比较控制器.circ as structural Verilog: 1 circuit, main circuit main
module main (
  input  [7:0] in_1,
  input  T2,
  input  T
);

  wire A_q, A_qn, and_1_out, and_2_out, and_3_out, and_4_out, and_5_out, and_6_out, and_7_out, B_q, B_qn,
       CAP_out, comparator_1_eq, comparator_1_gt, comparator_1_lt, LDA_out, LDB1_out, LDB2_out, or_1_out,
       or_2_out, or_3_out, or_4_out, xor_1_out;
  wire [7:0] A_2_q, B_2_q, controlled_buffer_1_out, controlled_buffer_2_out;

  D_Flip_Flop A (.clk(T), .D(or_2_out), .Q(A_q), .Qn(A_qn));  // open: preset, en, reset
  D_Flip_Flop B (.clk(T), .D(or_1_out), .Q(B_q), .Qn(B_qn));  // open: preset, en, reset
  or or_1 (or_1_out, B_qn, and_3_out);
  and and_1 (and_1_out, B_q, A_q);
  xor xor_1 (xor_1_out, A_q, B_q);
  or or_2 (or_2_out, xor_1_out, and_2_out);
  and LDB1 (LDB1_out, A_qn, B_qn);
  and and_2 (and_2_out, and_1_out, comparator_1_gt);
  and and_3 (and_3_out, and_1_out, or_4_out);
  and LDB2 (LDB2_out, A_q, B_qn);
  and LDA (LDA_out, A_qn, B_q);
  and CAP (CAP_out, A_q, B_q);
  Register A_2 (.D(B_2_q), .Q(A_2_q), .clk(and_4_out));  // open: en, clr
  and and_4 (and_4_out, T2, LDA_out);
  assign controlled_buffer_1_out = and_5_out ? A_2_q : 8'bz;  // Controlled_Buffer controlled_buffer_1
  and and_5 (and_5_out, T2, CAP_out);
  Register B_2 (.D(in_1), .Q(B_2_q), .clk(and_6_out));  // open: en, clr
  and and_6 (and_6_out, T2, or_3_out);
  or or_3 (or_3_out, LDB1_out, LDB2_out);
  assign controlled_buffer_2_out = and_7_out ? B_2_q : 8'bz;  // Controlled_Buffer controlled_buffer_2
  and and_7 (and_7_out, T2, CAP_out);
  Comparator comparator_1 (
    .a(controlled_buffer_1_out), .b(controlled_buffer_2_out), .gt(comparator_1_gt), .eq(comparator_1_eq),
    .lt(comparator_1_lt));
  or or_4 (or_4_out, comparator_1_eq, comparator_1_lt);
endmodule
