// Logisim project 计数器型累加器控制器.circ as structural Verilog: 1 circuit, main circuit main
module main (
  input  in_1,
  input  [7:0] in_2,
  input  T1,
  output out_4,
  output [7:0] out_5
);

  wire A_q, A_qn, adder_1_cout, and_1_out, and_2_out, and_3_out, and_4_out, and_5_out, B_q, B_qn, LDA_out,
       LDB_out, LDC_out, nCLK_out, not_1_out, or_1_out, or_2_out;
  wire [7:0] A_2_q, adder_1_out, controlled_buffer_1_out;

  not not_1 (not_1_out, T1);
  D_Flip_Flop A (.clk(T1), .D(or_1_out), .Q(A_q), .Qn(A_qn));  // open: preset, en, reset
  D_Flip_Flop B (.clk(T1), .D(or_2_out), .Q(B_q), .Qn(B_qn));  // open: preset, en, reset
  or or_1 (or_1_out, B_qn, A_qn);
  nor nCLK (nCLK_out, A_q, B_q);
  or or_2 (or_2_out, B_q, A_q);
  Register #(.width(1)) C (.D(adder_1_cout), .Q(out_4), .clk(and_1_out), .clr(nCLK_out));  // open: en
  and and_1 (and_1_out, not_1_out, LDC_out);
  and and_2 (and_2_out, not_1_out, LDA_out);
  xor LDB (LDB_out, B_q, A_q);
  and LDC (LDC_out, B_q, A_qn);
  Register A_2 (.D(in_2), .Q(A_2_q), .clk(and_2_out));  // open: en, clr
  or LDA (LDA_out, and_4_out, and_3_out);
  and and_3 (and_3_out, A_qn, B_qn);
  and and_4 (and_4_out, A_q, B_q);
  Adder adder_1 (.a(controlled_buffer_1_out), .b(A_2_q), .out(adder_1_out), .cin(in_1), .cout(adder_1_cout));
  Register B_2 (.D(adder_1_out), .Q(out_5), .clk(and_5_out), .clr(nCLK_out));  // open: en
  and and_5 (and_5_out, not_1_out, LDB_out);
  assign controlled_buffer_1_out = LDB_out ? out_5 : 8'bz;  // Controlled_Buffer controlled_buffer_1
endmodule
