// Logisim project de_selector.circ as structural Verilog: 1 circuit, main circuit main
module main (
);

  wire and_1_out, and_2_out, and_3_out, and_4_out, controlled_buffer_1_out, controlled_buffer_2_out,
       controlled_buffer_3_out, controlled_buffer_4_out, not_1_out, not_2_out, undriven, undriven_2,
       undriven_3, undriven_4;

  not not_1 (not_1_out, undriven_2);
  not not_2 (not_2_out, undriven);
  not not_3 (not_2_out, undriven_3);
  and and_1 (and_1_out, undriven_2, undriven_3, not_2_out);
  and and_2 (and_2_out, undriven_2, not_2_out, not_2_out);
  and and_3 (and_3_out, not_1_out, undriven_3, not_2_out);
  and and_4 (and_4_out, not_2_out, not_1_out, not_2_out);
  assign controlled_buffer_1_out = and_1_out ? undriven_4 : 1'bz;  // Controlled_Buffer controlled_buffer_1
  assign controlled_buffer_2_out = and_2_out ? undriven_4 : 1'bz;  // Controlled_Buffer controlled_buffer_2
  assign controlled_buffer_3_out = and_3_out ? undriven_4 : 1'bz;  // Controlled_Buffer controlled_buffer_3
  assign controlled_buffer_4_out = and_4_out ? undriven_4 : 1'bz;  // Controlled_Buffer controlled_buffer_4

  // Notes on the sheet:
  //   In
  //   S1
  //   S0
  //   C3
  //   C2
  //   C1
  //   C0
  //   Y3
  //   G3
  //   Y2
  //   G2
  //   Y1
  //   G1
  //   Y0
  //   G0
endmodule
