// Logisim project 多路选择器型累加器控制器 .circ as structural Verilog: 1 circuit, main circuit main
module main (
  input  in_1,
  input  [7:0] in_2,
  input  T1,
  output out_4,
  output [7:0] out_5
);

  wire A_qn, adder_1_cout, and_1_out, and_2_out, and_3_out, and_4_out, and_5_out, B_qn, LDA_out, LDB_out,
       LDC_out, multiplexer_1_out, multiplexer_2_out, nCLK_out, not_1_out;
  wire [1:0] A_q;
  wire [7:0] A_2_q, adder_1_out, controlled_buffer_1_out;

  Multiplexer #(.select(2)) multiplexer_1 (
    .in0(1'b1), .in1(1'b1), .in2(1'b1), .in3(1'b0), .out(multiplexer_1_out), .sel(A_q), .en(1'b1));
  Multiplexer #(.select(2)) multiplexer_2 (
    .in0(1'b0), .in1(1'b1), .in2(1'b1), .in3(1'b1), .out(multiplexer_2_out), .sel(A_q), .en(1'b1));
  not not_1 (not_1_out, T1);
  D_Flip_Flop A (.clk(T1), .D(multiplexer_1_out), .Q(A_q[0]), .Qn(A_qn));  // open: preset, en, reset
  D_Flip_Flop B (.clk(T1), .D(multiplexer_2_out), .Q(A_q[1]), .Qn(B_qn));  // open: preset, en, reset
  nor nCLK (nCLK_out, A_q[0], A_q[1]);
  Register #(.width(1)) C (.D(adder_1_cout), .Q(out_4), .clk(and_1_out), .clr(nCLK_out));  // open: en
  and and_1 (and_1_out, not_1_out, LDC_out);
  and and_2 (and_2_out, not_1_out, LDA_out);
  xor LDB (LDB_out, A_q[1], A_q[0]);
  and LDC (LDC_out, A_q[1], A_qn);
  Register A_2 (.D(in_2), .Q(A_2_q), .clk(and_2_out));  // open: en, clr
  or LDA (LDA_out, and_3_out, and_4_out);
  and and_3 (and_3_out, A_q[0], A_q[1]);
  and and_4 (and_4_out, A_qn, B_qn);
  Adder adder_1 (.a(controlled_buffer_1_out), .b(A_2_q), .out(adder_1_out), .cin(in_1), .cout(adder_1_cout));
  Register B_2 (.D(adder_1_out), .Q(out_5), .clk(and_5_out), .clr(nCLK_out));  // open: en
  and and_5 (and_5_out, not_1_out, LDB_out);
  assign controlled_buffer_1_out = LDB_out ? out_5 : 8'bz;  // Controlled_Buffer controlled_buffer_1
endmodule
