// Logisim project 定序型累加器控制器 .circ as structural Verilog: 1 circuit, main circuit main
module main (
  input  in_1,
  input  [7:0] in_2,
  input  T2,
  input  T1,
  output out_5,
  output [7:0] out_6
);

  wire a_q, a_qn, adder_1_cout, and_1_out, and_2_out, and_3_out, and_4_out, b_q, b_qn, c_q, c_qn, d_q, d_qn,
       LDA_out, LDB_out, or_1_out;
  wire [7:0] A_2_q, adder_1_out, controlled_buffer_1_out;

  and and_1 (and_1_out, d_qn, c_qn, b_qn, a_qn);
  D_Flip_Flop a (.clk(T1), .D(and_1_out), .Q(a_q), .Qn(a_qn));  // open: preset, en, reset
  D_Flip_Flop b (.clk(T1), .D(a_q), .Q(b_q), .Qn(b_qn));  // open: preset, en, reset
  or or_1 (or_1_out, b_q, d_q);
  D_Flip_Flop c (.clk(T1), .D(or_1_out), .Q(c_q), .Qn(c_qn));  // open: preset, en, reset
  D_Flip_Flop d (.clk(T1), .D(c_q), .Q(d_q), .Qn(d_qn));  // open: preset, en, reset
  and and_2 (and_2_out, T2, d_q);
  Register #(.width(1)) C_2 (.D(adder_1_cout), .Q(out_5), .clk(and_2_out), .clr(a_q));  // open: en
  Register A_2 (.D(in_2), .Q(A_2_q), .clk(and_3_out));  // open: en, clr
  and and_3 (and_3_out, T2, LDA_out);
  or LDB (LDB_out, b_q, d_q);
  Adder adder_1 (.a(controlled_buffer_1_out), .b(A_2_q), .out(adder_1_out), .cin(in_1), .cout(adder_1_cout));
  or LDA (LDA_out, a_q, c_q);
  and and_4 (and_4_out, T2, LDB_out);
  assign controlled_buffer_1_out = LDB_out ? out_6 : 8'bz;  // Controlled_Buffer controlled_buffer_1
  Register B_2 (.D(adder_1_out), .Q(out_6), .clk(and_4_out), .clr(a_q));  // open: en
endmodule
