// Logisim project 数字逻辑控制器.circ as structural Verilog: 1 circuit, main circuit main
module main (
  input  game_start,
  input  game_over,
  output A,
  output nA,
  output B,
  output nB
);

  wire and_1_out, and_2_out, and_3_out, and_4_out, not_1_out, or_1_out, or_2_out;

  not not_1 (not_1_out, game_over);
  and and_1 (and_1_out, nA, B, game_over);
  and and_2 (and_2_out, A, nB, game_start);
  and and_3 (and_3_out, nA, nB, game_start);
  and and_4 (and_4_out, nA, B, not_1_out);
  or or_1 (or_1_out, and_1_out, and_2_out);
  or or_2 (or_2_out, and_3_out, and_4_out);
  D_Flip_Flop u_A (.clk(or_1_out), .Q(A), .Qn(nA));  // open: D, preset, en, reset
  D_Flip_Flop u_B (.clk(or_2_out), .Q(B), .Qn(nB));  // open: D, preset, en, reset
endmodule
