// Logisim project Synchronous Mod-8 Counter 同步模8计数器.circ as structural Verilog: 1 circuit, main circuit main
module main (
  input  in_1,
  input  in_2,
  output out_3,
  output out_4,
  output out_5
);

  wire and_1_out, clock_1_out;

  Clock clock_1 (.out(clock_1_out));
  J_K_Flip_Flop j_k_ff_1 (.J(in_1), .clk(clock_1_out), .K(in_1), .Q(out_3), .en(in_2));  // open: Qn, preset, reset
  J_K_Flip_Flop j_k_ff_2 (.J(out_3), .clk(clock_1_out), .K(out_3), .Q(out_4), .en(in_2));  // open: Qn, preset, reset
  and and_1 (and_1_out, out_3, out_4);
  J_K_Flip_Flop j_k_ff_3 (
    .J(and_1_out), .clk(clock_1_out), .K(and_1_out), .Q(out_5), .en(in_2));  // open: Qn, preset, reset
endmodule
