// Logisim project 数字逻辑实验三.circ as structural Verilog: 1 circuit, main circuit main
module main (
  input  in_1,
  input  in_2,
  input  in_3,
  input  in_4,
  input  in_5,
  input  in_6,
  input  in_7,
  input  in_8,
  input  in_9,
  input  in_10,
  input  in_11,
  input  in_12,
  input  in_13,
  output out_14,
  output out_15,
  output out_16,
  output out_17,
  output out_18,
  output out_19,
  output out_20,
  output out_21,
  output out_22,
  output out_23,
  output out_24
);

  wire not_1_out, not_2_out, not_3_out, not_4_out;

  not not_1 (not_1_out, in_2);
  not not_2 (not_2_out, in_5);
  not not_3 (not_3_out, in_7);
  not not_4 (not_4_out, in_10);
  or or_1 (out_15, not_1_out, in_3, in_5, in_7, in_10);
  or or_2 (out_16, not_1_out, in_3, not_2_out, in_7, in_10);
  or or_3 (out_18, not_1_out, in_3, in_5, not_3_out, in_10);
  or or_4 (out_20, not_1_out, in_3, not_2_out, not_3_out, in_10);
  or or_5 (out_21, not_1_out, in_3, in_5, in_7, not_4_out);
  or or_6 (out_22, not_1_out, in_3, not_2_out, in_7, not_4_out);
  or or_7 (out_23, not_1_out, in_3, in_5, not_3_out, not_4_out);
  or or_8 (out_24, not_1_out, in_3, not_2_out, not_3_out, not_4_out);
  or or_9 (out_14, in_4, in_8, in_11, in_13);
  or or_10 (out_17, in_6, in_8, in_12, in_13);
  or or_11 (out_19, in_9, in_11, in_12, in_13);
endmodule
